# Fritzing sketch VirtualWire_tempalte (saved by Fritzing 0.9.3b)

parts:
  MicroBreadboard_left1 = prefix0000 [form="♀ (female)"]
  MicroBreadboard_right1 = MicroBreadbaord_right [form="♀ (female)"]
  Q1 = PNP-Transistor [package="TO92 [THT]"]
  D1 = Rectifier Diode [part_number=1N4001 package="300 mil [THT]"]
  R1 = Resistor [tolerance=±5% resistance=220 package=THT]

nets:
  N1: MicroBreadboard_left1.connector4, R1.Pin_0
  N2: MicroBreadboard_left1.connector9, MicroBreadboard_right1.connector36
  N3: MicroBreadboard_left1.connector14, MicroBreadboard_left1.connector29
  N4: MicroBreadboard_left1.connector34, MicroBreadboard_right1.connector22
  N5: MicroBreadboard_left1.connector39, D1.cathode
  N6: MicroBreadboard_right1.connector0, R1.Pin_1
  N7: MicroBreadboard_right1.connector1, MicroBreadboard_right1.connector11
  N8: MicroBreadboard_right1.connector10, Q1.C
  N9: MicroBreadboard_right1.connector12, MicroBreadboard_right1.connector17
  N10: MicroBreadboard_right1.connector15, Q1.B
  N11: MicroBreadboard_right1.connector20, Q1.E
  N12: MicroBreadboard_right1.connector35, D1.anode
